// Logisim project cpu.circ as structural Verilog: 1 circuit, main circuit cpu
module cpu (
  input  clk,
  input  [31:0] Instruction,
  input  [31:0] MemReadData,
  output [31:0] MemAddress,
  output [31:0] ProgramCounter,
  output [31:0] ra,
  output [31:0] sp,
  output [31:0] t0,
  output [31:0] t1,
  output [31:0] t2,
  output [31:0] s0,
  output [31:0] s1,
  output [31:0] a0,
  output [3:0] MemWriteMask,
  output [31:0] MemWriteData
);

  wire ASel, BrEq, BrLt, BrUn, BSel, MemRW, PCSel, RegWEn;
  wire [1:0] WBSel;
  wire [2:0] input_immsel;
  wire [3:0] input_alusel;
  wire [31:0] adder_1_out, input_B, output_alu, output_imm, output_rd1, output_rd2;

  Register #(.width(32)) PC (.D(adder_1_out), .clk(clk), .Q(ProgramCounter));  // open: en, clr
  Adder #(.width(32)) adder_1 (.a(ProgramCounter), .b(32'h4), .out(adder_1_out));  // open: cin, cout
  // Probe on Instruction
  // Probe on Instruction[11:7]
  // Probe on Instruction[19:15]
  // Probe on output_alu
  // Probe on RegWEn
  // Probe on input_immsel
  // Probe on input_alusel
  control_logic control_logic_1 (
    .Instruction(Instruction), .BrEq(BrEq), .BrLt(BrLt), .PCSel(PCSel), .RegWEn(RegWEn),
    .ImmSel(input_immsel), .BrUn(BrUn), .ASel(ASel), .BSel(BSel), .ALUSel(input_alusel), .MemRW(MemRW),
    .WBSel(WBSel));
  imm_gen imm_gen_1 (.Instruction(Instruction), .ImmSel(input_immsel), .Immediate(output_imm));
  regfile regfile_1 (
    .rs1(Instruction[19:15]), .rs2(Instruction[24:20]), .rd(Instruction[11:7]), .Write_Data(output_alu),
    .RegWEn(RegWEn), .clk(clk), .ra(ra), .sp(sp), .t0(t0), .t1(t1), .t2(t2), .s0(s0), .s1(s1), .a0(a0),
    .Read_Data_1(output_rd1), .Read_Data_2(output_rd2));
  Multiplexer #(.width(32)) multiplexer_1 (.in0(output_rd2), .in1(output_imm), .out(input_B), .sel(BSel));
  // branch_comp branch_comp_1: pin names not known
  alu alu_1 (.A(output_rd1), .B(input_B), .ALUSel(input_alusel), .ALUResult(output_alu));
  // partial_store partial_store_1: pin names not known
  // partial_load partial_load_1: pin names not known

  // Other names for the same wires on the sheet: input_rd[4:0] = Instruction[11:7];
  //   input_rs1[4:0] = Instruction[19:15]; input_rs2[4:0] = Instruction[24:20]

  // Notes on the sheet:
  //   To IMEM
  //   IMEM (do **NOT** move this)
  //   From IMEM
  //   Inputs/Outputs for testing. Do **NOT** move these.
  //   It is OK to move the PC, RegFile, ALU, MEM, Branch Comp, Imm Gen, Partial Load, Partial Store and Control Logic to wherever is most convenient for you when constructing your CPU, and to delete this text
  //   To DMEM
  //   DMEM (do **NOT** move this)
  //   From DMEM
endmodule
