// Logisim project partial-store.circ as structural Verilog: 1 circuit, main circuit partial_store
module partial_store (
  input  [31:0] Instruction,
  input  [31:0] MemAddress,
  input  [31:0] DataFromReg,
  input  MemRW,
  output [3:0] MemWriteMask,
  output [31:0] DataToMem
);

  wire and_1_out, and_2_out, comparator_1_eq, comparator_2_eq, comparator_3_eq, comparator_4_eq,
       comparator_5_eq, comparator_6_eq, comparator_7_eq, comparator_8_eq, comparator_9_eq, comparator_10_eq,
       sb0, sb1, sb2, sb3, sh0, sh2, sw0;

  Comparator #(.width(5)) comparator_1 (.a(Instruction[6:2]), .b(5'b01000), .eq(comparator_1_eq));  // open: gt, lt
  Comparator #(.width(3)) comparator_2 (.a(Instruction[14:12]), .b(3'b000), .eq(comparator_2_eq));  // open: gt, lt
  Comparator #(.width(2)) comparator_3 (.a(MemAddress[1:0]), .b(2'b00), .eq(comparator_3_eq));  // open: gt, lt
  Comparator #(.width(2)) comparator_4 (.a(MemAddress[1:0]), .b(2'b01), .eq(comparator_4_eq));  // open: gt, lt
  Comparator #(.width(2)) comparator_5 (.a(MemAddress[1:0]), .b(2'b10), .eq(comparator_5_eq));  // open: gt, lt
  Comparator #(.width(2)) comparator_6 (.a(MemAddress[1:0]), .b(2'b11), .eq(comparator_6_eq));  // open: gt, lt
  Comparator #(.width(3)) comparator_7 (.a(Instruction[14:12]), .b(3'b001), .eq(comparator_7_eq));  // open: gt, lt
  Comparator #(.width(2)) comparator_8 (.a(MemAddress[1:0]), .b(2'b00), .eq(comparator_8_eq));  // open: gt, lt
  Comparator #(.width(2)) comparator_9 (.a(MemAddress[1:0]), .b(2'b10), .eq(comparator_9_eq));  // open: gt, lt
  Comparator #(.width(3)) comparator_10 (.a(Instruction[14:12]), .b(3'b010), .eq(comparator_10_eq));  // open: gt, lt
  and and_1 (and_1_out, comparator_1_eq, comparator_2_eq);
  and and_2 (and_2_out, comparator_1_eq, comparator_7_eq);
  and and_3 (sw0, comparator_1_eq, comparator_10_eq);
  and and_4 (sb0, and_1_out, comparator_3_eq);
  and and_5 (sb1, and_1_out, comparator_4_eq);
  and and_6 (sb2, and_1_out, comparator_5_eq);
  and and_7 (sb3, and_1_out, comparator_6_eq);
  and and_8 (sh0, and_2_out, comparator_8_eq);
  and and_9 (sh2, and_2_out, comparator_9_eq);

  // Other names for the same wires on the sheet: opcode[4:0] = Instruction[6:2]; funct3[2:0] = Instruction[14:12];
  //   offset[1:0] = MemAddress[1:0]

  // Notes on the sheet:
  //   INPUTS to your circuit
  //   DON'T CHANGE THE LOCATIONS OF THE INPUTS AND OUTPUTS!
  //   OUTPUT from your circuit
endmodule
